// Logisim project Taekyu_Kim.circ as structural Verilog
module ALU (
  input  [31:0] RX,
  input  [31:0] RY,
  input  [1:0] func,
  output [31:0] RZ
);

  wire A___1, add, \nand , sub;
  wire [31:0] adder_1_out, adder_2_out, bit_extender_1_out, nand_1_out, subtractor_1_out;

  Decoder #(.select(2)) decoder_1 (.out0(add), .out1(\nand ), .out2(sub), .out3(A___1), .sel(func));  // open: en
  assign bit_extender_1_out = {{31{1'b0}}, 1'b1};  // Bit_Extender bit_extender_1
  Adder #(.width(32)) adder_1 (.a(RX), .b(RY), .out(adder_1_out));  // open: cin, cout
  assign nand_1_out = ~(RX & RY);  // NAND_Gate nand_1, 32 bits wide
  Subtractor #(.width(32)) subtractor_1 (.a(RX), .b(RY), .out(subtractor_1_out));  // open: bin, bout
  Adder #(.width(32)) adder_2 (.a(RX), .b(bit_extender_1_out), .out(adder_2_out));  // open: cin, cout
  Transistor #(.\type ("n"), .width(32)) transistor_1 (.in(adder_1_out), .out(RZ), .gate(add));
  Transistor #(.\type ("n"), .width(32)) transistor_2 (.in(nand_1_out), .out(RZ), .gate(\nand ));
  Transistor #(.\type ("n"), .width(32)) transistor_3 (.in(subtractor_1_out), .out(RZ), .gate(sub));
  Transistor #(.\type ("n"), .width(32)) transistor_4 (.in(adder_2_out), .out(RZ), .gate(A___1));
endmodule

module main1 (
  input  in_1,
  input  in_2,
  input  in_3,
  input  Clock,
  input  [4:0] in_5,
  input  in_6,
  output [31:0] out_7,
  output [3:0] out_8,
  output [5:0] out_9,
  output [31:0] out_10,
  output [31:0] out_11,
  output [31:0] out_12,
  output [5:0] out_13,
  output [11:0] out_14,
  output [11:0] out_15,
  output [1:0] out_16,
  output [23:0] out_17,
  output out_18,
  output [3:0] out_19,
  output [1:0] out_20,
  output [3:0] out_21,
  output [3:0] out_22,
  output [4:0] out_23
);

  wire comparator_1_eq, xor_1_out;
  wire [1:0] bit_extender_1_out, bit_extender_2_out, shifter_1_out;
  wire [6:0] Modifier_out_4;
  wire [11:0] bit_extender_4_out, shifter_2_out;
  wire [23:0] MAR_q;
  wire [31:0] ALU_rz, ldA_q, ldB_q, PC_q, ram_1_data, Registers_dout;

  assign bit_extender_1_out = {{1{1'b0}}, out_17[5]};  // Bit_Extender bit_extender_1
  assign bit_extender_2_out = {{1{1'b0}}, out_17[6]};  // Bit_Extender bit_extender_2
  assign out_7 = out_17[22] ? ALU_rz : 32'bz;  // Controlled_Buffer DrALU
  Shifter #(.width(2)) shifter_1 (.in(bit_extender_2_out), .\dist (1'b1), .out(shifter_1_out));
  Register #(.width(32)) PC (.D(out_7), .en(out_17[18]), .Q(PC_q), .clk(Clock), .clr(in_3));
  Modifier Modifier (.OP(out_11[31:26]), .M__T(out_16), .Z(out_18), .out_4(Modifier_out_4));
  assign out_16 = bit_extender_1_out | shifter_1_out;  // OR_Gate or_1, 2 bits wide
  Register #(.width(32)) ldB (.D(out_7), .en(out_17[16]), .Q(ldB_q), .clk(Clock));  // open: clr
  assign out_7 = out_17[23] ? PC_q : 32'bz;  // Controlled_Buffer DrPC
  assign out_14 = {{5{1'b0}}, Modifier_out_4};  // Bit_Extender bit_extender_3
  assign bit_extender_4_out = {{7{1'b0}}, out_23};  // Bit_Extender bit_extender_4
  Register #(.width(32)) ldA (.D(out_7), .en(out_17[17]), .Q(ldA_q), .clk(Clock));  // open: clr
  ALU ALU (.RX(ldA_q), .RY(ldB_q), .func(out_17[10:9]), .RZ(ALU_rz));
  Shifter #(.width(12)) shifter_2 (.in(out_14), .\dist (4'b0101), .out(shifter_2_out));
  assign out_15 = shifter_2_out | bit_extender_4_out;  // OR_Gate or_2, 12 bits wide
  Register #(.width(5)) State_Register (.D(out_17[4:0]), .Q(out_23), .clk(Clock), .clr(in_6));  // open: en
  Transistor transistor_1 (.in(1'b0), .out(out_17[5]), .gate(out_11[26]));
  Registers Registers (.Din(out_7), .Clock(Clock), .writeEn(out_17[11]), .regno(out_8), .Dout(Registers_dout));
  assign out_7 = out_17[21] ? Registers_dout : 32'bz;  // Controlled_Buffer DrREG
  ROM #(.addrWidth(12), .dataWidth(24)) rom_1 (.addr(out_15), .data(out_17));  // open: sel
  Register #(.width(32)) register_1 (.D(out_7), .en(out_17[14]), .Q(out_11), .clk(Clock));  // open: clr
  Transistor transistor_2 (.in(1'b0), .out(out_17[6]), .gate(out_11[26]));
  Register #(.width(24)) MAR (.D(out_7[23:0]), .en(out_17[15]), .Q(MAR_q), .clk(Clock), .clr(in_1));
  ROM #(.addrWidth(24), .dataWidth(32)) rom_2 ();  // open: addr, data, sel
  Transistor #(.\type ("n"), .width(32)) transistor_3 (.in(ram_1_data), .out(out_7), .gate(out_17[12]));
  RAM #(.addrWidth(24), .dataWidth(32)) ram_1 (
    .addr(MAR_q), .data(ram_1_data), .clk(Clock), .ld(xor_1_out), .clr(in_2));  // open: sel
  xor xor_1 (xor_1_out, 1'b1, out_17[12]);
  assign out_10 = {{12{1'b0}}, out_11[31:12]};  // Bit_Extender bit_extender_5
  assign out_7 = out_17[19] ? out_10 : 32'bz;  // Controlled_Buffer DrOFF
  assign out_7 = out_17[20] ? ram_1_data : 32'bz;  // Controlled_Buffer DrMEM
  Comparator #(.width(32)) comparator_1 (.a(out_7), .b({32{1'b0}}), .eq(comparator_1_eq));  // open: gt, lt
  Multiplexer #(.select(2), .width(4)) multiplexer_1 (
    .in0(out_11[25:22]), .in1(out_11[21:18]), .in2(out_11[3:0]), .in3(4'b0000), .out(out_8),
    .sel(out_17[8:7]), .en(1'b1));
  Register #(.width(1)) register_2 (.D(comparator_1_eq), .en(out_17[13]), .Q(out_18), .clk(Clock));  // open: clr

  assign out_12 = out_7;
  assign out_13 = out_11[31:26];
  assign out_19 = out_8;
  assign out_20 = out_17[8:7];
  assign out_21 = out_11[3:0];
  assign out_22 = out_11[25:22];

  // Other names for the same wires on the sheet: C = Clock; MT[1:0] = out_16; Rz[3:0] = out_11[3:0];
  //   Ry[3:0] = out_11[21:18]; Rx[3:0] = out_11[25:22]; OP[5:0] = out_11[31:26]; T = out_17[5]; M = out_17[6];
  //   RegSel[1:0] = out_17[8:7]; func[1:0] = out_17[10:9]; WrREG = out_17[11]; WrMEM = out_17[12]; LdZ = out_17[13];
  //   LdIR = out_17[14]; LdMAR = out_17[15]; LdB = out_17[16]; LdA = out_17[17]; LdPC = out_17[18];
  //   DrOFF = out_17[19]; DrMEM = out_17[20]; DrREG = out_17[21]; DrALU = out_17[22]; DrPC = out_17[23];
  //   regno[3:0] = out_8; z = out_18

  // Notes on the sheet:
  //   contents of rom_1 (hex, n*v repeats v):
  //   828001 104002 440643 220084 210105 400800 61*0 220084 210105 400a00 61*0 220084 90005 400800 61*0
  //   220084 90005 408006 100800 60*0 220084 90005 408006 201000 124*0 800884 240005 62*0 220084 210105
  //   400c00 61*0 220084 90005 c00 61*0 220004 400e00
  //   contents of rom_2 (hex, n*v repeats v):
  //   100002 24800000
endmodule

module Registers (
  input  [31:0] Din,
  input  Clock,
  input  writeEn,
  input  [3:0] regno,
  output [31:0] Dout
);

  wire _1, _2, _3, _4, _5, _6, _7, _8, _9, _10, _11, _12, _13, _14, _15, _16;
  wire [31:0] register_1_q, register_2_q, register_3_q, register_4_q, register_5_q, register_6_q,
       register_7_q, register_8_q, register_9_q, register_10_q, register_11_q, register_12_q, register_13_q,
       register_14_q, register_15_q, register_16_q, transistor_1_out, transistor_2_out, transistor_3_out,
       transistor_4_out, transistor_5_out, transistor_6_out, transistor_7_out, transistor_8_out,
       transistor_17_out, transistor_18_out, transistor_19_out, transistor_20_out, transistor_21_out,
       transistor_22_out, transistor_23_out, transistor_24_out;

  Transistor #(.\type ("n"), .width(32)) transistor_1 (.in(Din), .out(transistor_1_out), .gate(_1));
  Transistor #(.\type ("n"), .width(32)) transistor_2 (.in(Din), .out(transistor_2_out), .gate(_2));
  Register #(.width(32)) register_1 (.D(transistor_2_out), .en(writeEn), .Q(register_1_q), .clk(Clock));  // open: clr
  Register #(.width(32)) register_2 (.D(transistor_3_out), .en(writeEn), .Q(register_2_q), .clk(Clock));  // open: clr
  Transistor #(.\type ("n"), .width(32)) transistor_3 (.in(Din), .out(transistor_3_out), .gate(_3));
  Transistor #(.\type ("n"), .width(32)) transistor_4 (.in(Din), .out(transistor_4_out), .gate(_4));
  Register #(.width(32)) register_3 (.D(transistor_4_out), .en(writeEn), .Q(register_3_q), .clk(Clock));  // open: clr
  Transistor #(.\type ("n"), .width(32)) transistor_5 (.in(Din), .out(transistor_5_out), .gate(_5));
  Register #(.width(32)) register_4 (.D(transistor_5_out), .en(writeEn), .Q(register_4_q), .clk(Clock));  // open: clr
  Transistor #(.\type ("n"), .width(32)) transistor_6 (.in(Din), .out(transistor_6_out), .gate(_6));
  Register #(.width(32)) register_5 (.D(transistor_6_out), .en(writeEn), .Q(register_5_q), .clk(Clock));  // open: clr
  Register #(.width(32)) register_6 (.D(transistor_7_out), .en(writeEn), .Q(register_6_q), .clk(Clock));  // open: clr
  Transistor #(.\type ("n"), .width(32)) transistor_7 (.in(Din), .out(transistor_7_out), .gate(_7));
  Transistor #(.\type ("n"), .width(32)) transistor_8 (.in(Din), .out(transistor_8_out), .gate(_8));
  Transistor #(.\type ("n"), .width(32)) transistor_9 (.in(register_7_q), .out(Dout), .gate(_1));
  Register #(.width(32)) register_7 (.D(transistor_1_out), .en(writeEn), .Q(register_7_q), .clk(Clock));  // open: clr
  Transistor #(.\type ("n"), .width(32)) transistor_10 (.in(register_1_q), .out(Dout), .gate(_2));
  Transistor #(.\type ("n"), .width(32)) transistor_11 (.in(register_2_q), .out(Dout), .gate(_3));
  Transistor #(.\type ("n"), .width(32)) transistor_12 (.in(register_3_q), .out(Dout), .gate(_4));
  Transistor #(.\type ("n"), .width(32)) transistor_13 (.in(register_4_q), .out(Dout), .gate(_5));
  Transistor #(.\type ("n"), .width(32)) transistor_14 (.in(register_5_q), .out(Dout), .gate(_6));
  Transistor #(.\type ("n"), .width(32)) transistor_15 (.in(register_6_q), .out(Dout), .gate(_7));
  Transistor #(.\type ("n"), .width(32)) transistor_16 (.in(register_8_q), .out(Dout), .gate(_8));
  Register #(.width(32)) register_8 (.D(transistor_8_out), .en(writeEn), .Q(register_8_q), .clk(Clock));  // open: clr
  Register #(.width(32)) register_9 (.D(transistor_17_out), .en(writeEn), .Q(register_9_q), .clk(Clock));  // open: clr
  Transistor #(.\type ("n"), .width(32)) transistor_17 (.in(Din), .out(transistor_17_out), .gate(_9));
  Register #(.width(32)) register_10 (
    .D(transistor_18_out), .en(writeEn), .Q(register_10_q), .clk(Clock));  // open: clr
  Transistor #(.\type ("n"), .width(32)) transistor_18 (.in(Din), .out(transistor_18_out), .gate(_10));
  Transistor #(.\type ("n"), .width(32)) transistor_19 (.in(Din), .out(transistor_19_out), .gate(_11));
  Register #(.width(32)) register_11 (
    .D(transistor_19_out), .en(writeEn), .Q(register_11_q), .clk(Clock));  // open: clr
  Register #(.width(32)) register_12 (
    .D(transistor_20_out), .en(writeEn), .Q(register_12_q), .clk(Clock));  // open: clr
  Transistor #(.\type ("n"), .width(32)) transistor_20 (.in(Din), .out(transistor_20_out), .gate(_12));
  Transistor #(.\type ("n"), .width(32)) transistor_21 (.in(Din), .out(transistor_21_out), .gate(_13));
  Register #(.width(32)) register_13 (
    .D(transistor_21_out), .en(writeEn), .Q(register_13_q), .clk(Clock));  // open: clr
  Transistor #(.\type ("n"), .width(32)) transistor_22 (.in(Din), .out(transistor_22_out), .gate(_14));
  Register #(.width(32)) register_14 (
    .D(transistor_22_out), .en(writeEn), .Q(register_14_q), .clk(Clock));  // open: clr
  Register #(.width(32)) register_15 (
    .D(transistor_23_out), .en(writeEn), .Q(register_15_q), .clk(Clock));  // open: clr
  Transistor #(.\type ("n"), .width(32)) transistor_23 (.in(Din), .out(transistor_23_out), .gate(_15));
  Transistor #(.\type ("n"), .width(32)) transistor_24 (.in(Din), .out(transistor_24_out), .gate(_16));
  Register #(.width(32)) register_16 (
    .D(transistor_24_out), .en(writeEn), .Q(register_16_q), .clk(Clock));  // open: clr
  Transistor #(.\type ("n"), .width(32)) transistor_25 (.in(register_9_q), .out(Dout), .gate(_9));
  Transistor #(.\type ("n"), .width(32)) transistor_26 (.in(register_10_q), .out(Dout), .gate(_10));
  Transistor #(.\type ("n"), .width(32)) transistor_27 (.in(register_11_q), .out(Dout), .gate(_11));
  Transistor #(.\type ("n"), .width(32)) transistor_28 (.in(register_12_q), .out(Dout), .gate(_12));
  Transistor #(.\type ("n"), .width(32)) transistor_29 (.in(register_13_q), .out(Dout), .gate(_13));
  Transistor #(.\type ("n"), .width(32)) transistor_30 (.in(register_14_q), .out(Dout), .gate(_14));
  Transistor #(.\type ("n"), .width(32)) transistor_31 (.in(register_15_q), .out(Dout), .gate(_15));
  Transistor #(.\type ("n"), .width(32)) transistor_32 (.in(register_16_q), .out(Dout), .gate(_16));
  Decoder #(.select(4)) decoder_1 (
    .out0(_1), .out1(_2), .out2(_3), .out3(_4), .out4(_5), .out5(_6), .out6(_7), .out7(_8), .out8(_9),
    .out9(_10), .out10(_11), .out11(_12), .out12(_13), .out13(_14), .out14(_15), .out15(_16), .sel(regno));  // open: en

  // Other names for the same wires on the sheet: C = Clock; W = writeEn
endmodule

module Modifier (
  input  [5:0] OP,
  input  [1:0] M__T,
  input  Z,
  output [6:0] out_4
);

  wire Z_t;
  wire [5:0] OP_t;
  wire [6:0] bit_extender_1_out, bit_extender_2_out, shifter_1_out;

  Transistor #(.\type ("n"), .width(6)) transistor_1 (.in(OP), .out(OP_t), .gate(M__T[0]));
  Transistor #(.width(6)) transistor_2 (.in({6{1'b0}}), .out(OP_t), .gate(M__T[0]));
  Transistor #(.\type ("n")) transistor_3 (.in(Z), .out(Z_t), .gate(M__T[1]));
  Transistor transistor_4 (.in(1'b0), .out(Z_t), .gate(M__T[1]));
  assign bit_extender_1_out = {{1{1'b0}}, OP_t};  // Bit_Extender bit_extender_1
  assign bit_extender_2_out = {{6{1'b0}}, Z_t};  // Bit_Extender bit_extender_2
  Shifter #(.width(7)) shifter_1 (.in(bit_extender_1_out), .\dist (3'b001), .out(shifter_1_out));
  assign out_4 = shifter_1_out | bit_extender_2_out;  // OR_Gate or_1, 7 bits wide

  // Other names for the same wires on the sheet: M = M__T[0]; T = M__T[1]
endmodule

module oh (
  input  [1:0] in_1,
  input  in_2,
  input  in_3,
  input  C,
  input  in_5,
  input  ld,
  output [1:0] out_7,
  output [1:0] out_8,
  output [1:0] out_9
);

  wire [1:0] register_1_q;

  Register #(.width(2)) register_1 (.D(in_1), .en(in_2), .Q(register_1_q), .clk(in_3));  // open: clr
  RAM #(.addrWidth(2), .dataWidth(2)) ram_1 (.addr(register_1_q), .data(out_7), .clk(C), .ld(ld));  // open: sel, clr
  Transistor #(.width(2)) transistor_1 (.in(out_7), .out(in_1), .gate(ld));
  assign in_1 = in_5 ? out_7 : 2'bz;  // Controlled_Buffer controlled_buffer_1

  assign out_8 = in_1;
  assign out_9 = in_1;
endmodule
