// Logisim project LC-2200-32.circ as structural Verilog: 7 circuits, main circuit Processor
module Processor (
  input  [3:0] in_1,
  output [31:0] out_2,
  output [31:0] out_3,
  output [31:0] out_4,
  output [3:0] out_5,
  output [31:0] out_6,
  output [1:0] out_7
);

  wire Clock, Clr, DrALU, DrEnInt, DrMEM, DrOFF, DrPC, DrReg, IE, IntAck, Interrupt, intSignal, LdA, LdB,
       LdEnInt, LdIR, LdMAR, LdPC, LdZ, not_1_out, register_1_q, register_2_q, transistor_1_out, WrMEM,
       WrREG, Z, ZeroDetectOut;
  wire [1:0] FUNC;
  wire [23:0] bit_extender_1_out, DeviceInd, MAR_q, transistor_3_out;
  wire [31:0] A_q, B_q, ram_1_data, registers_1_data_out, ZeroDetect;

  Intergenerator Intergenerator (.IntOut(Interrupt), .CLK(Clock));
  PC PC (.in_1(out_2), .LdPC(LdPC), .Clock(Clock), .Output(out_3), .Clr(Clr));
  assign out_2 = DrPC ? out_3 : 32'bz;  // Controlled_Buffer controlled_buffer_1
  State_Machine state_machine_1 (
    .Clock(Clock), .OpCode(out_4[31:28]), .Z(Z), .IE(IE), .Int_Signal(intSignal), .DrREG(DrReg),
    .DrMEM(DrMEM), .DrALU(DrALU), .DrPC(DrPC), .DrOFF(DrOFF), .LdPC(LdPC), .LdIR(LdIR), .LdMAR(LdMAR),
    .LdA(LdA), .LdB(LdB), .LdZ(LdZ), .WrREG(WrREG), .WrMEM(WrMEM), .RegSel(out_7), .ALU_FUNC(FUNC),
    .LdEnInt(LdEnInt), .DrEnInt(DrEnInt), .IntAck(IntAck));
  Register #(.width(32)) A (.D(out_2), .en(LdA), .Q(A_q), .clk(Clock), .clr(Clr));
  Register #(.width(1)) Z_Register (.D(ZeroDetectOut), .en(LdZ), .Q(Z), .clk(Clock), .clr(Clr));
  ALU alu_1 (.FUNC(FUNC), .INPUT_A(A_q), .INPUT_B(B_q), .out_4(ZeroDetect));
  assign out_2 = DrALU ? ZeroDetect : 32'bz;  // Controlled_Buffer controlled_buffer_2
  Transistor #(.\type ("n")) transistor_1 (.in(1'b1), .out(transistor_1_out), .gate(LdEnInt));
  Transistor #(.\type ("n")) transistor_2 (.in(1'b0), .out(transistor_1_out), .gate(DrEnInt));
  Register #(.width(32)) B (.D(out_2), .en(LdB), .Q(B_q), .clk(Clock), .clr(Clr));
  Clock clock_1 (.out(Clock));
  Button button_1 (.out(Clr));
  Register #(.width(1)) u_IE (.D(transistor_1_out), .Q(IE), .clk(Clock));  // open: en, clr
  Registers registers_1 (
    .WrReg(WrREG), .RegSel(out_5), .Data_In(out_2), .Clock(Clock), .ClearRegFile(Clr),
    .Data_Out(registers_1_data_out));
  assign out_2 = DrReg ? registers_1_data_out : 32'bz;  // Controlled_Buffer controlled_buffer_3
  Transistor #(.width(24)) transistor_3 (.in(MAR_q), .out(transistor_3_out), .gate(IntAck));
  Register #(.width(1)) register_1 (.D(Interrupt), .en(Interrupt), .Q(register_1_q), .clk(Clock), .clr(IntAck));
  Register #(.width(24)) MAR (.D(out_2[23:0]), .en(LdMAR), .Q(MAR_q), .clk(Clock), .clr(Clr));
  Transistor #(.\type ("n"), .width(24)) transistor_4 (.in(DeviceInd), .out(transistor_3_out), .gate(IntAck));
  Register #(.width(1)) register_2 (.D(intSignal), .Q(register_2_q));  // open: en, clk, clr
  Transistor transistor_5 (.in(register_1_q), .out(intSignal), .gate(IntAck));
  RAM #(.addrWidth(24), .dataWidth(32), .bus("separate")) ram_1 (
    .addr(transistor_3_out), .din(out_2), .data(ram_1_data), .str(WrMEM), .clk(Clock), .ld(not_1_out),
    .clr(Clr));  // open: sel
  not not_1 (not_1_out, WrMEM);
  assign out_2 = DrMEM ? ram_1_data : 32'bz;  // Controlled_Buffer controlled_buffer_4
  Comparator #(.width(32), .mode("unsigned")) comparator_1 (
    .a(ZeroDetect), .b({32{1'b0}}), .eq(ZeroDetectOut));  // open: gt, lt
  assign bit_extender_1_out = {{23{1'b0}}, register_2_q};  // Bit_Extender bit_extender_1
  Register #(.width(32)) IR (.D(out_2), .en(LdIR), .Q(out_4), .clk(Clock), .clr(Clr));
  Multiplexer #(.select(2), .width(4), .enable("false")) multiplexer_1 (
    .in0(out_4[27:24]), .in1(out_4[23:20]), .in2(out_4[3:0]), .in3(4'b1100), .out(out_5), .sel(out_7));
  assign out_2 = DrOFF ? {{13{out_4[19]}}, out_4[18:0]} : 32'bz;  // Controlled_Buffer controlled_buffer_5
  Transistor #(.width(24)) transistor_6 (.in(bit_extender_1_out), .out(DeviceInd), .gate(IntAck));

  assign out_6 = out_2;

  // Other names for the same wires on the sheet: Opcode[3:0] = out_4[31:28]; Reg_num[3:0] = out_5;
  //   RegSel[1:0] = out_7

  // Notes on the sheet:
  //   00 = RX
  //   01 = RY
  //   10 = RZ
  //   11 = $k0
endmodule

module ALU (
  input  [31:0] INPUT_A,
  input  [31:0] INPUT_B,
  input  [1:0] FUNC,
  output [31:0] out_4
);

  wire [31:0] adder_1_out, adder_2_out, nand_1_out, subtractor_1_out;

  Adder #(.width(32)) adder_1 (.a(INPUT_A), .b(INPUT_B), .out(adder_1_out));  // open: cin, cout
  assign nand_1_out = ~(INPUT_A & INPUT_B);  // NAND_Gate nand_1, 32 bits wide
  Multiplexer #(.select(2), .width(32), .enable("false")) multiplexer_1 (
    .in0(adder_1_out), .in1(nand_1_out), .in2(subtractor_1_out), .in3(adder_2_out), .out(out_4), .sel(FUNC));
  Subtractor #(.width(32)) subtractor_1 (.a(INPUT_A), .b(INPUT_B), .out(subtractor_1_out));  // open: bin, bout
  Adder #(.width(32)) adder_2 (.a(INPUT_A), .b(32'h1), .out(adder_2_out));  // open: cin, cout
endmodule

module State_Machine (
  input  Clock,
  input  [3:0] OpCode,
  input  Z,
  input  IE,
  input  Int_Signal,
  output DrREG,
  output DrMEM,
  output DrALU,
  output DrPC,
  output DrOFF,
  output LdPC,
  output LdIR,
  output LdMAR,
  output LdA,
  output LdB,
  output LdZ,
  output WrREG,
  output WrMEM,
  output [1:0] RegSel,
  output [1:0] ALU_FUNC,
  output LdEnInt,
  output DrEnInt,
  output IntAck
);

  wire chkZ, OpTest;
  wire [5:0] multiplexer_1_out, register_1_q, rom_1_data, rom_2_data, rom_3_data, rom_4_data;

  Register #(.width(6)) register_1 (.D(multiplexer_1_out), .en(Clock), .Q(register_1_q), .clk(Clock));  // open: clr
  Multiplexer #(.select(2), .width(6), .enable("false")) multiplexer_1 (
    .in0(rom_1_data), .in1(rom_2_data), .in2(rom_3_data), .in3(rom_4_data), .out(multiplexer_1_out),
    .sel({chkZ, OpTest}));
  ROM #(.addrWidth(6), .dataWidth(28)) rom_1 (
    .addr(register_1_q),
    .data({IntAck, DrEnInt, LdEnInt, chkZ, OpTest, ALU_FUNC, RegSel, WrMEM, WrREG, LdZ, LdB, LdA, LdMAR, LdIR, LdPC, DrOFF, DrPC, DrALU, DrMEM, DrREG, rom_1_data}));  // open: sel
  ROM #(.addrWidth(4), .dataWidth(6)) rom_2 (.addr(OpCode), .data(rom_2_data));  // open: sel
  ROM #(.addrWidth(2), .dataWidth(6)) rom_3 (.addr({1'b0, Z}), .data(rom_3_data));  // open: sel
  ROM #(.addrWidth(2), .dataWidth(6)) rom_4 (.addr({Int_Signal, IE}), .data(rom_4_data));  // open: sel

  // Notes on the sheet:
  //   contents of rom_1 (hex, n*v repeats v):
  //   1800004 21a0202 8002003 897 4205 602906 801087 84048 108049 20100 8404b 10804c 220100 8404e 840f
  //   20100 84051 8412 2113 20080 84055 8416 2117 40040 4059 8805a 41011b 1000000 421d 841e 900 a0220 840
  //   2000000 4000000 180815 24
  //   contents of rom_2 (hex, n*v repeats v):
  //   7 a d 10 14 18 1f 21 22 23 24
  //   contents of rom_3 (hex, n*v repeats v):
  //   0 1e
  //   contents of rom_4 (hex, n*v repeats v):
  //   4 4 4 1
endmodule

// 0?
module Zero_Detection (
  input  [31:0] In,
  output Out
);

  Comparator #(.width(32), .mode("unsigned")) comparator_1 (.a(In), .b({32{1'b0}}), .eq(Out));  // open: gt, lt
endmodule

// Reg File
module Registers (
  input  [31:0] Data_In,
  input  WrReg,
  input  [3:0] RegSel,
  input  Clock,
  input  ClearRegFile,
  output [31:0] Data_Out
);

  wire and_1_out, and_2_out, and_3_out, and_4_out, and_5_out, and_6_out, and_7_out, and_8_out, and_9_out,
       and_10_out, and_11_out, and_12_out, and_13_out, and_14_out, and_15_out, and_16_out, decoder_1_out0,
       decoder_1_out1, decoder_1_out2, decoder_1_out3, decoder_1_out4, decoder_1_out5, decoder_1_out6,
       decoder_1_out7, decoder_1_out8, decoder_1_out9, decoder_1_out10, decoder_1_out11, decoder_1_out12,
       decoder_1_out13, decoder_1_out14, decoder_1_out15;
  wire [31:0] a0, a1, a2, at, k0, pr, ra, s0, s1, s2, sp, t0, t1, t2, v0, zero;

  Decoder #(.select(4), .enable("false")) decoder_1 (
    .out0(decoder_1_out0), .out1(decoder_1_out1), .out2(decoder_1_out2), .out3(decoder_1_out3),
    .out4(decoder_1_out4), .out5(decoder_1_out5), .out6(decoder_1_out6), .out7(decoder_1_out7),
    .out8(decoder_1_out8), .out9(decoder_1_out9), .out10(decoder_1_out10), .out11(decoder_1_out11),
    .out12(decoder_1_out12), .out13(decoder_1_out13), .out14(decoder_1_out14), .out15(decoder_1_out15),
    .sel(RegSel));
  and and_1 (and_1_out, decoder_1_out0, WrReg);
  and and_2 (and_2_out, decoder_1_out1, WrReg);
  and and_3 (and_3_out, decoder_1_out2, WrReg);
  and and_4 (and_4_out, decoder_1_out3, WrReg);
  and and_5 (and_5_out, decoder_1_out4, WrReg);
  and and_6 (and_6_out, decoder_1_out5, WrReg);
  and and_7 (and_7_out, decoder_1_out6, WrReg);
  and and_8 (and_8_out, decoder_1_out7, WrReg);
  and and_9 (and_9_out, decoder_1_out8, WrReg);
  and and_10 (and_10_out, decoder_1_out9, WrReg);
  and and_11 (and_11_out, decoder_1_out10, WrReg);
  and and_12 (and_12_out, decoder_1_out11, WrReg);
  and and_13 (and_13_out, decoder_1_out12, WrReg);
  and and_14 (and_14_out, decoder_1_out13, WrReg);
  and and_15 (and_15_out, decoder_1_out14, WrReg);
  and and_16 (and_16_out, decoder_1_out15, WrReg);
  Register #(.width(32)) u_zero (.D(Data_In), .en(and_1_out), .Q(zero), .clk(Clock), .clr(1'b1));
  Register #(.width(32)) u_at (.D(Data_In), .en(and_2_out), .Q(at), .clk(Clock), .clr(ClearRegFile));
  Register #(.width(32)) u_v0 (.D(Data_In), .en(and_3_out), .Q(v0), .clk(Clock), .clr(ClearRegFile));
  Register #(.width(32)) u_a0 (.D(Data_In), .en(and_4_out), .Q(a0), .clk(Clock), .clr(ClearRegFile));
  Register #(.width(32)) u_a1 (.D(Data_In), .en(and_5_out), .Q(a1), .clk(Clock), .clr(ClearRegFile));
  Register #(.width(32)) u_a2 (.D(Data_In), .en(and_6_out), .Q(a2), .clk(Clock), .clr(ClearRegFile));
  Register #(.width(32)) u_t0 (.D(Data_In), .en(and_7_out), .Q(t0), .clk(Clock), .clr(ClearRegFile));
  Register #(.width(32)) u_t1 (.D(Data_In), .en(and_8_out), .Q(t1), .clk(Clock), .clr(ClearRegFile));
  Register #(.width(32)) u_t2 (.D(Data_In), .en(and_9_out), .Q(t2), .clk(Clock), .clr(ClearRegFile));
  Register #(.width(32)) u_s0 (.D(Data_In), .en(and_10_out), .Q(s0), .clk(Clock), .clr(ClearRegFile));
  Register #(.width(32)) u_s1 (.D(Data_In), .en(and_11_out), .Q(s1), .clk(Clock), .clr(ClearRegFile));
  Register #(.width(32)) u_s2 (.D(Data_In), .en(and_12_out), .Q(s2), .clk(Clock), .clr(ClearRegFile));
  Register #(.width(32)) u_k0 (.D(Data_In), .en(and_13_out), .Q(k0), .clk(Clock), .clr(ClearRegFile));
  Register #(.width(32)) u_sp (.D(Data_In), .en(and_14_out), .Q(sp), .clk(Clock), .clr(ClearRegFile));
  Register #(.width(32)) u_pr (.D(Data_In), .en(and_15_out), .Q(pr), .clk(Clock), .clr(ClearRegFile));
  Register #(.width(32)) u_ra (.D(Data_In), .en(and_16_out), .Q(ra), .clk(Clock), .clr(ClearRegFile));
  Multiplexer #(.select(4), .width(32), .enable("false")) multiplexer_1 (
    .in0(zero), .in1(at), .in2(v0), .in3(a0), .in4(a1), .in5(a2), .in6(t0), .in7(t1), .in8(t2), .in9(s0),
    .in10(s1), .in11(s2), .in12(k0), .in13(sp), .in14(pr), .in15(ra), .out(Data_Out), .sel(RegSel));

  // Other names for the same wires on the sheet: Din[31:0] = Data_In; en = WrReg
endmodule

module Intergenerator (
  input  CLK,
  output IntOut
);

  wire register_2_q;
  wire [10:0] adder_1_out, register_1_q;

  Adder #(.width(11)) adder_1 (.a(11'h1), .b(register_1_q), .out(adder_1_out));  // open: cin, cout
  Register #(.width(11)) register_1 (.D(adder_1_out), .en(1'b1), .Q(register_1_q), .clk(CLK), .clr(register_2_q));
  Comparator #(.width(11), .mode("unsigned")) comparator_1 (
    .a(11'h200), .b(register_1_q), .eq(IntOut));  // open: gt, lt
  Register #(.width(1)) register_2 (.D(IntOut), .en(1'b1), .Q(register_2_q), .clk(CLK), .clr(register_2_q));
endmodule

module PC (
  input  [31:0] in_1,
  input  LdPC,
  input  Clock,
  input  Clr,
  output [31:0] Output
);

  wire comparator_1_eq, comparator_1_gt, comparator_1_lt;
  wire [31:0] transistor_1_out;

  Comparator #(.width(32)) comparator_1 (
    .a(in_1), .b(32'hf), .gt(comparator_1_gt), .eq(comparator_1_eq), .lt(comparator_1_lt));
  Transistor #(.\type ("n"), .width(32)) transistor_1 (.in(32'hf), .out(transistor_1_out), .gate(comparator_1_lt));
  Transistor #(.\type ("n"), .width(32)) transistor_2 (.in(in_1), .out(transistor_1_out), .gate(comparator_1_gt));
  Transistor #(.\type ("n"), .width(32)) transistor_3 (.in(32'hf), .out(transistor_1_out), .gate(comparator_1_eq));
  Register #(.width(32)) PC (.D(transistor_1_out), .en(LdPC), .Q(Output), .clk(Clock), .clr(Clr));

  // Other names for the same wires on the sheet: Data[31:0] = in_1
endmodule
