// Logisim project project3_2.circ as structural Verilog: 9 circuits, main circuit ALU
module ALU (
  input  [31:0] INPUT_A,
  input  [31:0] INPUT_B,
  input  [1:0] FUNC,
  output [31:0] Output
);

  wire [31:0] adder_1_out, adder_2_out, nand_1_out, subtractor_1_out;

  Adder #(.width(32)) adder_1 (.a(INPUT_A), .b(INPUT_B), .out(adder_1_out));  // open: cin, cout
  assign nand_1_out = ~(INPUT_A & INPUT_B);  // NAND_Gate nand_1, 32 bits wide
  Multiplexer #(.select(2), .width(32), .enable("false")) multiplexer_1 (
    .in0(adder_1_out), .in1(nand_1_out), .in2(subtractor_1_out), .in3(adder_2_out), .out(Output), .sel(FUNC));
  Subtractor #(.width(32)) subtractor_1 (.a(INPUT_A), .b(INPUT_B), .out(subtractor_1_out));  // open: bin, bout
  Adder #(.width(32)) adder_2 (.a(INPUT_A), .b(32'h1), .out(adder_2_out));  // open: cin, cout
endmodule

module DPRF (
  input  WrReg,
  input  [3:0] regsel1,
  input  [3:0] regsel2,
  input  [3:0] regsel0,
  input  [3:0] wrReg0,
  input  clock,
  input  clr,
  input  [31:0] wrReg0Val,
  output [31:0] reg1val,
  output [31:0] reg2val,
  output [31:0] reg0val,
  output [3:0] regsel1Out
);

  Registers2 registers2_1 (
    .WrReg(WrReg), .RegSel1(regsel1), .RegSel2(regsel2), .RegSel0(regsel0), .wrReg0(wrReg0),
    .reg0DataIn(wrReg0Val), .Clock(clock), .ClearRegFile(clr), .Data_Out1(reg1val), .Data_Out2(reg2val),
    .Data_Out0(reg0val));

  assign regsel1Out = regsel1;
endmodule

module main (
  input  in_1,
  input  in_2
);

  wire adder_2_out, and_2_out, checkNoop, clock, comparator_1_eq, EXBuffer_wrreg0out, EXBuffer_wrregmemout,
       flushing, FordReg0, FordReg1, FordReg2, IDBuffer_wrmem, IDBuffer_wrreg0out, IDBuffer_wrregmemout,
       Noop, NoopClock, opBEQ, or_5_out, useImm, WrMem, WrReg0, WrRegMem;
  wire [1:0] ALUfun, nextPC;
  wire [2:0] Forwarding_wbreg0out, Forwarding_wbreg1out, Forwarding_wbreg2out;
  wire [3:0] DPRF_regsel1out, EXBuffer_reg0out, IDBuffer_reg0_2, IDBuffer_regsel1out, MEMBuffer_reg0out,
       multiplexer_9_out, reg0, reg1, reg2;
  wire [7:0] multiplexer_2_out_2;
  wire [19:0] IDBuffer_imm_2;
  wire [23:0] multiplexer_2_out, PC_q;
  wire [31:0] ADD_2_output, ADD_output, bit_extender_1_out, bit_extender_2_out, bit_extender_3_out,
       controlled_buffer_1_out, DPRF_reg0val, DPRF_reg1val, DPRF_reg2val, EXBuffer_aluout,
       EXBuffer_reg0dataout, Forwarding_exout, Forwarding_memout, Forwarding_wbout, IDBuffer_pcout,
       IDBuffer_reg0valout, IDBuffer_reg1_2, IFBuffer_pcout, MEMBuffer_memout, MEMBuffer_regout,
       multiplexer_3_out, multiplexer_4_out, multiplexer_5_out, multiplexer_6_out, multiplexer_7_out,
       multiplexer_8_out, multiplexer_10_out, multiplexer_11_out, multiplexer_12_out, rom_1_data, ZeroDetect;
  wire [31:4] IFBuffer_irout;

  Register #(.width(24)) PC (.D(multiplexer_2_out), .Q(PC_q), .clk(clock));  // open: en, clr
  Clock clock_1 (.out(clock));
  Comparator #(.width(32), .mode("unsigned")) comparator_1 (
    .a(ZeroDetect), .b({32{1'b0}}), .eq(comparator_1_eq));  // open: gt, lt
  assign bit_extender_1_out = {{8{1'b0}}, PC_q};  // Bit_Extender bit_extender_1
  ALU ADD (.FUNC(2'b11), .INPUT_A(bit_extender_1_out), .Output(ADD_output));  // open: INPUT_B
  Multiplexer #(.enable("false")) multiplexer_1 (.in0(1'b0), .in1(comparator_1_eq), .out(nextPC[1]), .sel(opBEQ));
  or or_1 (flushing, nextPC[0], nextPC[1]);
  Multiplexer #(.select(2), .width(32), .enable("false")) multiplexer_2 (
    .in0(ADD_output), .in1(IDBuffer_pcout), .in2(ADD_2_output),
    .out({multiplexer_2_out_2, multiplexer_2_out}), .sel(nextPC));  // open: in3
  ROM #(.addrWidth(24), .dataWidth(32)) rom_1 (.addr(PC_q), .data(rom_1_data));  // open: sel
  and and_1 (NoopClock, clock, Noop);
  IFBuffer IFBuffer (
    .PCin(ADD_output), .clock(NoopClock), .clr(flushing), .IRin(rom_1_data), .PCout(IFBuffer_pcout),
    .IRout({IFBuffer_irout[31:28], reg0, reg1, IFBuffer_irout[19:4], reg2}));  // open: en
  Multiplexer #(.width(32), .enable("false")) multiplexer_3 (
    .in0(DPRF_reg2val), .in1(multiplexer_6_out), .out(multiplexer_3_out), .sel(FordReg2));
  Multiplexer #(.width(32), .enable("false")) multiplexer_4 (
    .in0(DPRF_reg0val), .in1(multiplexer_7_out), .out(multiplexer_4_out), .sel(FordReg0));
  DPRF DPRF (
    .WrReg(WrReg0), .regsel1(reg1), .regsel2(reg2), .regsel0(reg0), .wrReg0(MEMBuffer_reg0out),
    .wrReg0Val(multiplexer_12_out), .clock(clock), .clr(flushing), .reg1val(DPRF_reg1val),
    .reg2val(DPRF_reg2val), .reg0val(DPRF_reg0val), .regsel1Out(DPRF_regsel1out));
  Multiplexer #(.select(3), .width(32), .enable("false")) multiplexer_5 (
    .in1(Forwarding_wbout), .in2(Forwarding_memout), .in3(Forwarding_memout), .in4(Forwarding_exout),
    .in5(Forwarding_exout), .in6(Forwarding_exout), .in7(Forwarding_exout), .out(multiplexer_5_out),
    .sel(Forwarding_wbreg1out));  // open: in0
  Multiplexer #(.select(3), .width(32), .enable("false")) multiplexer_6 (
    .in1(Forwarding_wbout), .in2(Forwarding_memout), .in3(Forwarding_memout), .in4(Forwarding_exout),
    .in5(Forwarding_exout), .in6(Forwarding_exout), .in7(Forwarding_exout), .out(multiplexer_6_out),
    .sel(Forwarding_wbreg2out));  // open: in0
  or or_2 (FordReg2, Forwarding_wbreg2out[2], Forwarding_wbreg2out[1], Forwarding_wbreg2out[0]);
  Multiplexer #(.select(3), .width(32), .enable("false")) multiplexer_7 (
    .in1(Forwarding_wbout), .in2(Forwarding_memout), .in3(Forwarding_memout), .in4(Forwarding_exout),
    .in5(Forwarding_exout), .in6(Forwarding_exout), .in7(Forwarding_exout), .out(multiplexer_7_out),
    .sel(Forwarding_wbreg0out));  // open: in0
  Multiplexer #(.width(32), .enable("false")) multiplexer_8 (
    .in0(DPRF_reg1val), .in1(multiplexer_5_out), .out(multiplexer_8_out), .sel(FordReg1));
  or or_3 (FordReg1, Forwarding_wbreg1out[2], Forwarding_wbreg1out[1], Forwarding_wbreg1out[0]);
  or or_4 (FordReg0, Forwarding_wbreg0out[2], Forwarding_wbreg0out[1], Forwarding_wbreg0out[0]);
  IDBuffer IDBuffer (
    .clock(NoopClock), .reg1(multiplexer_8_out), .reg2(multiplexer_3_out),
    .imm({IFBuffer_irout[19:4], reg2}), .PCin(IFBuffer_pcout), .reg0(reg0), .reg0valIn(multiplexer_4_out),
    .OpIn(IFBuffer_irout[31:28]), .regsel1In(DPRF_regsel1out), .reg1_2(IDBuffer_reg1_2),
    .reg2_2(IDBuffer_reg1_2), .imm_2(IDBuffer_imm_2), .PCout(IDBuffer_pcout), .reg0_2(IDBuffer_reg0_2),
    .reg0valOut(IDBuffer_reg0valout), .ALUfunc(ALUfun), .useImm(useImm), .opJALR(nextPC[0]), .opBEQ(opBEQ),
    .regsel1Out(IDBuffer_regsel1out), .Noop(checkNoop), .WrMEM(IDBuffer_wrmem),
    .WrRegMemOut(IDBuffer_wrregmemout), .WrReg0Out(IDBuffer_wrreg0out));  // open: WrEn
  Forwarding Forwarding (
    .reg1(reg1), .reg2(reg2), .EXreg0in(multiplexer_9_out), .MEMreg0in(EXBuffer_reg0out),
    .WBreg0in(MEMBuffer_reg0out), .EXin(ZeroDetect), .MEMin(EXBuffer_reg0dataout), .WBin(multiplexer_12_out),
    .reg0(reg0), .EXreg1out(Forwarding_wbreg1out[2]), .EXreg2out(Forwarding_wbreg2out[2]),
    .MEMreg1out(Forwarding_wbreg1out[1]), .MEMreg2out(Forwarding_wbreg2out[1]),
    .WBreg1out(Forwarding_wbreg1out[0]), .WBreg2out(Forwarding_wbreg2out[0]),
    .EXreg0out(Forwarding_wbreg0out[2]), .MEMreg0out(Forwarding_wbreg0out[1]),
    .WBreg0out(Forwarding_wbreg0out[0]), .EXout(Forwarding_exout), .MEMout(Forwarding_memout),
    .WBout(Forwarding_wbout));
  or or_5 (or_5_out, FordReg1, FordReg2);
  assign bit_extender_2_out = {{12{1'b0}}, IDBuffer_imm_2};  // Bit_Extender bit_extender_2
  ALU ADD_2 (.FUNC(2'b00), .INPUT_A(IDBuffer_pcout), .INPUT_B(bit_extender_2_out), .Output(ADD_2_output));
  assign bit_extender_3_out = {{12{1'b0}}, IDBuffer_imm_2};  // Bit_Extender bit_extender_3
  Multiplexer #(.width(4), .enable("false")) multiplexer_9 (
    .in0(IDBuffer_reg0_2), .in1(IDBuffer_regsel1out), .out(multiplexer_9_out), .sel(nextPC[0]));
  and and_2 (and_2_out, checkNoop, or_5_out);
  Multiplexer #(.select(2), .width(32), .enable("false")) multiplexer_10 (
    .in0(IDBuffer_reg1_2), .in1(bit_extender_3_out), .in2(IDBuffer_reg0valout), .out(multiplexer_10_out),
    .sel({opBEQ, useImm}));  // open: in3
  Adder #(.width(1)) adder_1 (.a(1'b1), .b(and_2_out), .out(Noop));  // open: cin, cout
  ALU alu_1 (.FUNC(ALUfun), .INPUT_A(IDBuffer_reg1_2), .INPUT_B(multiplexer_10_out), .Output(ZeroDetect));
  Multiplexer #(.width(32), .enable("false")) multiplexer_11 (
    .in0(IDBuffer_pcout), .in1(ZeroDetect), .out(multiplexer_11_out), .sel(nextPC[0]));
  EXBuffer EXBuffer (
    .clock(clock), .ALUin(multiplexer_11_out), .reg0(multiplexer_9_out), .reg0DataIn(IDBuffer_reg0valout),
    .WrMEMIn(IDBuffer_wrmem), .WrRegMemIn(IDBuffer_wrregmemout), .WrReg0In(IDBuffer_wrreg0out),
    .ALUout(EXBuffer_aluout), .reg0Out(EXBuffer_reg0out), .reg0DataOut(EXBuffer_reg0dataout), .WrMEM(WrMem),
    .WrRegMemOut(EXBuffer_wrregmemout), .WrReg0Out(EXBuffer_wrreg0out));  // open: WrEn
  assign controlled_buffer_1_out = WrMem ? EXBuffer_reg0dataout : 32'bz;  // Controlled_Buffer controlled_buffer_1
  RAM #(.addrWidth(24), .dataWidth(32)) ram_1 (
    .addr(EXBuffer_aluout[31:8]), .data(controlled_buffer_1_out), .clk(clock), .ld(adder_2_out));  // open: sel, clr
  Adder #(.width(1)) adder_2 (.a(WrMem), .b(in_1), .out(adder_2_out));  // open: cin, cout
  MEMBuffer MEMBuffer (
    .clock(clock), .MemIn(controlled_buffer_1_out), .RegIn(EXBuffer_reg0dataout), .reg0in(EXBuffer_reg0out),
    .WrRegMemIn(EXBuffer_wrregmemout), .WrReg0In(EXBuffer_wrreg0out), .MemOut(MEMBuffer_memout),
    .RegOut(MEMBuffer_regout), .reg0out(MEMBuffer_reg0out), .WrRegMemOut(WrRegMem), .WrReg0Out(WrReg0));  // open: WrEn, clear, Reg0DataIn, Reg0DataOut
  Multiplexer #(.width(32), .enable("false")) multiplexer_12 (
    .in0(MEMBuffer_regout), .in1(MEMBuffer_memout), .out(multiplexer_12_out), .sel(WrRegMem));

  // Other names for the same wires on the sheet: opJALR = nextPC[0]; ZeroDetectOut = nextPC[1]

  // Notes on the sheet:
  //   contents of rom_1 (hex, n*v repeats v):
  //   3000000 2400000b 53400002 43300000 23300001
endmodule

module IFBuffer (
  input  [31:0] PCin,
  input  en,
  input  clock,
  input  clr,
  input  [31:0] IRin,
  output [31:0] PCout,
  output [31:0] IRout
);

  wire multiplexer_1_out, multiplexer_2_out;
  wire [31:0] register_1_q, register_2_q;

  Register #(.width(32)) register_1 (.D(PCin), .en(en), .Q(register_1_q), .clk(clock), .clr(clr));
  Register #(.width(32)) register_2 (.D(IRin), .en(en), .Q(register_2_q), .clk(clock), .clr(clr));
  assign PCout = multiplexer_1_out ? register_1_q : 32'bz;  // Controlled_Buffer controlled_buffer_1
  Multiplexer #(.enable("false")) multiplexer_1 (.in0(1'b1), .in1(1'b0), .out(multiplexer_1_out), .sel(clock));
  assign IRout = multiplexer_2_out ? register_2_q : 32'bz;  // Controlled_Buffer controlled_buffer_2
  Multiplexer #(.enable("false")) multiplexer_2 (.in0(1'b1), .in1(1'b0), .out(multiplexer_2_out), .sel(clock));
endmodule

module IDBuffer (
  input  clock,
  input  WrEn,
  input  [31:0] reg1,
  input  [31:0] reg2,
  input  [19:0] imm,
  input  [31:0] PCin,
  input  [3:0] reg0,
  input  [31:0] reg0valIn,
  input  [3:0] OpIn,
  input  [3:0] regsel1In,
  output [31:0] reg1_2,
  output [31:0] reg2_2,
  output [19:0] imm_2,
  output [31:0] PCout,
  output [3:0] reg0_2,
  output [31:0] reg0valOut,
  output [1:0] ALUfunc,
  output useImm,
  output opJALR,
  output opBEQ,
  output [3:0] regsel1Out,
  output Noop,
  output WrMEM,
  output WrRegMemOut,
  output WrReg0Out
);

  wire multiplexer_1_out, multiplexer_2_out, multiplexer_3_out, multiplexer_4_out, multiplexer_5_out,
       multiplexer_6_out, multiplexer_7_out;
  wire [3:0] controlled_buffer_1_out, register_1_q, register_6_q;
  wire [19:0] register_4_q;
  wire [31:0] register_2_q, register_3_q, register_5_q, register_7_q;

  assign controlled_buffer_1_out = multiplexer_1_out ? register_1_q : 4'bz;  // Controlled_Buffer controlled_buffer_1
  Register #(.width(4)) register_1 (.D(OpIn), .en(WrEn), .Q(register_1_q), .clk(clock));  // open: clr
  Multiplexer #(.enable("false")) multiplexer_1 (.in0(1'b1), .in1(1'b0), .out(multiplexer_1_out), .sel(clock));
  assign reg1_2 = multiplexer_2_out ? register_2_q : 32'bz;  // Controlled_Buffer controlled_buffer_2
  Register #(.width(32)) register_2 (.D(reg1), .en(WrEn), .Q(register_2_q), .clk(clock));  // open: clr
  Multiplexer #(.enable("false")) multiplexer_2 (.in0(1'b1), .in1(1'b0), .out(multiplexer_2_out), .sel(clock));
  Register #(.width(32)) register_3 (.D(reg2), .en(WrEn), .Q(register_3_q), .clk(clock));  // open: clr
  assign reg2_2 = multiplexer_3_out ? register_3_q : 32'bz;  // Controlled_Buffer controlled_buffer_3
  Multiplexer #(.enable("false")) multiplexer_3 (.in0(1'b1), .in1(1'b0), .out(multiplexer_3_out), .sel(clock));
  assign imm_2 = multiplexer_4_out ? register_4_q : 20'bz;  // Controlled_Buffer controlled_buffer_4
  Register #(.width(20)) register_4 (.D(imm), .en(WrEn), .Q(register_4_q), .clk(clock));  // open: clr
  Multiplexer #(.enable("false")) multiplexer_4 (.in0(1'b1), .in1(1'b0), .out(multiplexer_4_out), .sel(clock));
  assign PCout = multiplexer_6_out ? register_5_q : 32'bz;  // Controlled_Buffer controlled_buffer_5
  Register #(.width(32)) register_5 (.D(PCin), .en(WrEn), .Q(register_5_q), .clk(clock));  // open: clr
  Register #(.width(4)) register_6 (.D(reg0), .en(WrEn), .Q(register_6_q), .clk(clock));  // open: clr
  assign reg0_2 = multiplexer_5_out ? register_6_q : 4'bz;  // Controlled_Buffer controlled_buffer_6
  Multiplexer #(.enable("false")) multiplexer_5 (.in0(1'b1), .in1(1'b0), .out(multiplexer_5_out), .sel(clock));
  Register #(.width(32)) register_7 (.D(reg0valIn), .en(WrEn), .Q(register_7_q), .clk(clock));  // open: clr
  ROM #(.addrWidth(4), .dataWidth(9)) rom_1 (
    .addr(controlled_buffer_1_out),
    .data({ALUfunc, useImm, opJALR, opBEQ, Noop, WrMEM, WrRegMemOut, WrReg0Out}));  // open: sel
  Multiplexer #(.enable("false")) multiplexer_6 (.in0(1'b1), .in1(1'b0), .out(multiplexer_6_out), .sel(clock));
  assign reg0valOut = multiplexer_7_out ? register_7_q : 32'bz;  // Controlled_Buffer controlled_buffer_7
  Multiplexer #(.enable("false")) multiplexer_7 (.in0(1'b1), .in1(1'b0), .out(multiplexer_7_out), .sel(clock));
  Register #(.width(4)) register_8 (.D(regsel1In), .en(WrEn), .Q(regsel1Out), .clk(clock));  // open: clr

  // Notes on the sheet:
  //   contents of rom_1 (hex, n*v repeats v):
  //   1 81 41 4b 44 110 21
endmodule

module EXBuffer (
  input  clock,
  input  WrEn,
  input  [31:0] ALUin,
  input  [3:0] reg0,
  input  [31:0] reg0DataIn,
  input  WrMEMIn,
  input  WrRegMemIn,
  input  WrReg0In,
  output [31:0] ALUout,
  output [3:0] reg0Out,
  output [31:0] reg0DataOut,
  output WrMEM,
  output WrRegMemOut,
  output WrReg0Out
);

  wire multiplexer_1_out, multiplexer_2_out, multiplexer_3_out, multiplexer_4_out, multiplexer_5_out,
       multiplexer_6_out, register_3_q, register_4_q, register_5_q;
  wire [3:0] register_1_q;
  wire [31:0] register_2_q, register_6_q;

  Register #(.width(4)) register_1 (.D(reg0), .en(WrEn), .Q(register_1_q), .clk(clock));  // open: clr
  Register #(.width(32)) register_2 (.D(reg0DataIn), .en(WrEn), .Q(register_2_q), .clk(clock));  // open: clr
  Register #(.width(1)) register_3 (.D(WrMEMIn), .en(WrEn), .Q(register_3_q), .clk(clock));  // open: clr
  Register #(.width(1)) register_4 (.D(WrRegMemIn), .en(WrEn), .Q(register_4_q), .clk(clock));  // open: clr
  Register #(.width(1)) register_5 (.D(WrReg0In), .en(WrEn), .Q(register_5_q), .clk(clock));  // open: clr
  Register #(.width(32)) register_6 (.D(ALUin), .en(WrEn), .Q(register_6_q), .clk(clock));  // open: clr
  assign ALUout = multiplexer_1_out ? register_6_q : 32'bz;  // Controlled_Buffer controlled_buffer_1
  Multiplexer #(.enable("false")) multiplexer_1 (.in0(1'b1), .in1(1'b0), .out(multiplexer_1_out), .sel(clock));
  assign reg0Out = multiplexer_2_out ? register_1_q : 4'bz;  // Controlled_Buffer controlled_buffer_2
  Multiplexer #(.enable("false")) multiplexer_2 (.in0(1'b1), .in1(1'b0), .out(multiplexer_2_out), .sel(clock));
  assign reg0DataOut = multiplexer_3_out ? register_2_q : 32'bz;  // Controlled_Buffer controlled_buffer_3
  Multiplexer #(.enable("false")) multiplexer_3 (.in0(1'b1), .in1(1'b0), .out(multiplexer_3_out), .sel(clock));
  assign WrMEM = multiplexer_4_out ? register_3_q : 1'bz;  // Controlled_Buffer controlled_buffer_4
  Multiplexer #(.enable("false")) multiplexer_4 (.in0(1'b1), .in1(1'b0), .out(multiplexer_4_out), .sel(clock));
  assign WrRegMemOut = multiplexer_5_out ? register_4_q : 1'bz;  // Controlled_Buffer controlled_buffer_5
  Multiplexer #(.enable("false")) multiplexer_5 (.in0(1'b1), .in1(1'b0), .out(multiplexer_5_out), .sel(clock));
  assign WrReg0Out = multiplexer_6_out ? register_5_q : 1'bz;  // Controlled_Buffer controlled_buffer_6
  Multiplexer #(.enable("false")) multiplexer_6 (.in0(1'b1), .in1(1'b0), .out(multiplexer_6_out), .sel(clock));
endmodule

module MEMBuffer (
  input  clock,
  input  WrEn,
  input  clear,
  input  [31:0] MemIn,
  input  [31:0] RegIn,
  input  [3:0] reg0in,
  input  [31:0] Reg0DataIn,
  input  WrRegMemIn,
  input  WrReg0In,
  output [31:0] MemOut,
  output [31:0] RegOut,
  output [3:0] reg0out,
  output [31:0] Reg0DataOut,
  output WrRegMemOut,
  output WrReg0Out
);

  wire multiplexer_1_out, multiplexer_2_out, multiplexer_3_out, multiplexer_4_out, multiplexer_5_out,
       multiplexer_6_out, register_5_q, register_6_q;
  wire [3:0] register_3_q;
  wire [31:0] register_1_q, register_2_q, register_4_q;

  Register #(.width(32)) register_1 (.D(MemIn), .en(WrEn), .Q(register_1_q), .clk(clock), .clr(clear));
  Register #(.width(32)) register_2 (.D(RegIn), .en(WrEn), .Q(register_2_q), .clk(clock), .clr(clear));
  Register #(.width(4)) register_3 (.D(reg0in), .en(WrEn), .Q(register_3_q), .clk(clock), .clr(clear));
  assign Reg0DataOut = multiplexer_1_out ? register_4_q : 32'bz;  // Controlled_Buffer controlled_buffer_1
  Register #(.width(32)) register_4 (.D(Reg0DataIn), .en(WrEn), .Q(register_4_q), .clk(clock), .clr(clear));
  Multiplexer #(.enable("false")) multiplexer_1 (.in0(1'b1), .in1(1'b0), .out(multiplexer_1_out), .sel(clock));
  Register #(.width(1)) register_5 (.D(WrRegMemIn), .en(WrEn), .Q(register_5_q), .clk(clock), .clr(clear));
  assign WrRegMemOut = multiplexer_6_out ? register_5_q : 1'bz;  // Controlled_Buffer controlled_buffer_2
  Register #(.width(1)) register_6 (.D(WrReg0In), .en(WrEn), .Q(register_6_q), .clk(clock), .clr(clear));
  assign WrReg0Out = multiplexer_2_out ? register_6_q : 1'bz;  // Controlled_Buffer controlled_buffer_3
  Multiplexer #(.enable("false")) multiplexer_2 (.in0(1'b1), .in1(1'b0), .out(multiplexer_2_out), .sel(clock));
  assign MemOut = multiplexer_3_out ? register_1_q : 32'bz;  // Controlled_Buffer controlled_buffer_4
  Multiplexer #(.enable("false")) multiplexer_3 (.in0(1'b1), .in1(1'b0), .out(multiplexer_3_out), .sel(clock));
  assign RegOut = multiplexer_4_out ? register_2_q : 32'bz;  // Controlled_Buffer controlled_buffer_5
  Multiplexer #(.enable("false")) multiplexer_4 (.in0(1'b1), .in1(1'b0), .out(multiplexer_4_out), .sel(clock));
  assign reg0out = multiplexer_5_out ? register_3_q : 4'bz;  // Controlled_Buffer controlled_buffer_6
  Multiplexer #(.enable("false")) multiplexer_5 (.in0(1'b1), .in1(1'b0), .out(multiplexer_5_out), .sel(clock));
  Multiplexer #(.enable("false")) multiplexer_6 (.in0(1'b1), .in1(1'b0), .out(multiplexer_6_out), .sel(clock));

  // Other names for the same wires on the sheet: clr = clear
endmodule

module Forwarding (
  input  [3:0] reg1,
  input  [3:0] reg2,
  input  [3:0] EXreg0in,
  input  [3:0] MEMreg0in,
  input  [3:0] WBreg0in,
  input  [31:0] EXin,
  input  [31:0] MEMin,
  input  [31:0] WBin,
  input  [3:0] reg0,
  output EXreg1out,
  output EXreg2out,
  output MEMreg1out,
  output MEMreg2out,
  output WBreg1out,
  output WBreg2out,
  output EXreg0out,
  output MEMreg0out,
  output WBreg0out,
  output [31:0] EXout,
  output [31:0] MEMout,
  output [31:0] WBout
);

  Comparator #(.width(4)) comparator_1 (.a(EXreg0in), .b(reg1), .eq(EXreg1out));  // open: gt, lt
  Comparator #(.width(4)) comparator_2 (.a(EXreg0in), .b(reg2), .eq(EXreg2out));  // open: gt, lt
  Comparator #(.width(4)) comparator_3 (.a(EXreg0in), .b(reg0), .eq(EXreg0out));  // open: gt, lt
  Comparator #(.width(4)) comparator_4 (.a(MEMreg0in), .b(reg1), .eq(MEMreg1out));  // open: gt, lt
  Comparator #(.width(4)) comparator_5 (.a(MEMreg0in), .b(reg2), .eq(MEMreg2out));  // open: gt, lt
  Comparator #(.width(4)) comparator_6 (.a(MEMreg0in), .b(reg0), .eq(MEMreg0out));  // open: gt, lt
  Comparator #(.width(4)) comparator_7 (.a(WBreg0in), .b(reg1), .eq(WBreg1out));  // open: gt, lt
  Comparator #(.width(4)) comparator_8 (.a(WBreg0in), .b(reg2), .eq(WBreg2out));  // open: gt, lt
  Comparator #(.width(4)) comparator_9 (.a(WBreg0in), .b(reg0), .eq(WBreg0out));  // open: gt, lt

  assign EXout = EXin;
  assign MEMout = MEMin;
  assign WBout = WBin;
endmodule

module Registers2 (
  input  WrReg,
  input  [3:0] RegSel1,
  input  [3:0] RegSel2,
  input  [3:0] RegSel0,
  input  [3:0] wrReg0,
  input  Clock,
  input  ClearRegFile,
  input  [31:0] reg0DataIn,
  output [31:0] Data_Out1,
  output [31:0] Data_Out2,
  output [31:0] Data_Out0
);

  wire and_1_out, and_2_out, and_3_out, and_4_out, and_5_out, and_6_out, and_7_out, and_8_out, and_9_out,
       and_10_out, and_11_out, and_12_out, and_13_out, and_14_out, and_15_out, and_16_out, decoder_1_out0,
       decoder_1_out1, decoder_1_out2, decoder_1_out3, decoder_1_out4, decoder_1_out5, decoder_1_out6,
       decoder_1_out7, decoder_1_out8, decoder_1_out9, decoder_1_out10, decoder_1_out11, decoder_1_out12,
       decoder_1_out13, decoder_1_out14, decoder_1_out15;
  wire [31:0] a0, a1, a2, at, k0, pr, ra, s0, s1, s2, t0, t1, t2, v0, zero;

  Decoder #(.select(4), .enable("false")) decoder_1 (
    .out0(decoder_1_out0), .out1(decoder_1_out1), .out2(decoder_1_out2), .out3(decoder_1_out3),
    .out4(decoder_1_out4), .out5(decoder_1_out5), .out6(decoder_1_out6), .out7(decoder_1_out7),
    .out8(decoder_1_out8), .out9(decoder_1_out9), .out10(decoder_1_out10), .out11(decoder_1_out11),
    .out12(decoder_1_out12), .out13(decoder_1_out13), .out14(decoder_1_out14), .out15(decoder_1_out15),
    .sel(wrReg0));
  and and_1 (and_1_out, decoder_1_out0, WrReg);
  and and_2 (and_2_out, decoder_1_out1, WrReg);
  and and_3 (and_3_out, decoder_1_out2, WrReg);
  and and_4 (and_4_out, decoder_1_out3, WrReg);
  and and_5 (and_5_out, decoder_1_out4, WrReg);
  and and_6 (and_6_out, decoder_1_out5, WrReg);
  and and_7 (and_7_out, decoder_1_out6, WrReg);
  and and_8 (and_8_out, decoder_1_out7, WrReg);
  and and_9 (and_9_out, decoder_1_out8, WrReg);
  and and_10 (and_10_out, decoder_1_out9, WrReg);
  and and_11 (and_11_out, decoder_1_out10, WrReg);
  and and_12 (and_12_out, decoder_1_out11, WrReg);
  and and_13 (and_13_out, decoder_1_out12, WrReg);
  and and_14 (and_14_out, decoder_1_out13, WrReg);
  and and_15 (and_15_out, decoder_1_out14, WrReg);
  and and_16 (and_16_out, decoder_1_out15, WrReg);
  Register #(.width(32)) u_zero (.D(reg0DataIn), .en(and_1_out), .Q(zero), .clk(Clock), .clr(1'b1));
  Register #(.width(32)) u_at (.D(reg0DataIn), .en(and_2_out), .Q(at), .clk(Clock), .clr(ClearRegFile));
  Register #(.width(32)) u_v0 (.D(reg0DataIn), .en(and_3_out), .Q(v0), .clk(Clock), .clr(ClearRegFile));
  Register #(.width(32)) u_a0 (.D(reg0DataIn), .en(and_4_out), .Q(a0), .clk(Clock), .clr(ClearRegFile));
  Register #(.width(32)) u_a1 (.D(reg0DataIn), .en(and_5_out), .Q(a1), .clk(Clock), .clr(ClearRegFile));
  Register #(.width(32)) u_a2 (.D(reg0DataIn), .en(and_6_out), .Q(a2), .clk(Clock), .clr(ClearRegFile));
  Register #(.width(32)) u_t0 (.D(reg0DataIn), .en(and_7_out), .Q(t0), .clk(Clock), .clr(ClearRegFile));
  Register #(.width(32)) u_t1 (.D(reg0DataIn), .en(and_8_out), .Q(t1), .clk(Clock), .clr(ClearRegFile));
  Register #(.width(32)) u_t2 (.D(reg0DataIn), .en(and_9_out), .Q(t2), .clk(Clock), .clr(ClearRegFile));
  Register #(.width(32)) u_s0 (.D(reg0DataIn), .en(and_10_out), .Q(s0), .clk(Clock), .clr(ClearRegFile));
  Register #(.width(32)) u_s1 (.D(reg0DataIn), .en(and_11_out), .Q(s1), .clk(Clock), .clr(ClearRegFile));
  Register #(.width(32)) u_s2 (.D(reg0DataIn), .en(and_12_out), .Q(s2), .clk(Clock), .clr(ClearRegFile));
  Register #(.width(32)) u_k0 (.D(reg0DataIn), .en(and_13_out), .Q(k0), .clk(Clock), .clr(ClearRegFile));
  Register #(.width(32)) sp (.D(reg0DataIn), .en(and_14_out), .Q(pr), .clk(Clock), .clr(ClearRegFile));
  Register #(.width(32)) u_pr (.D(reg0DataIn), .en(and_15_out), .Q(pr), .clk(Clock), .clr(ClearRegFile));
  Register #(.width(32)) u_ra (.D(reg0DataIn), .en(and_16_out), .Q(ra), .clk(Clock), .clr(ClearRegFile));
  Multiplexer #(.select(4), .width(32), .enable("false")) multiplexer_1 (
    .in0(zero), .in1(at), .in2(v0), .in3(a0), .in4(a1), .in5(a2), .in6(t0), .in7(t1), .in8(t2), .in9(s0),
    .in10(s1), .in11(s2), .in12(k0), .in13(pr), .in14(pr), .in15(ra), .out(Data_Out1), .sel(RegSel1));
  Multiplexer #(.select(4), .width(32), .enable("false")) multiplexer_2 (
    .in0(zero), .in1(at), .in2(v0), .in3(a0), .in4(a1), .in5(a2), .in6(t0), .in7(t1), .in8(t2), .in9(s0),
    .in10(s1), .in11(s2), .in12(k0), .in13(pr), .in14(pr), .in15(ra), .out(Data_Out2), .sel(RegSel2));
  Multiplexer #(.select(4), .width(32), .enable("false")) multiplexer_3 (
    .in0(zero), .in1(at), .in2(v0), .in3(a0), .in4(a1), .in5(a2), .in6(t0), .in7(t1), .in8(t2), .in9(s0),
    .in10(s1), .in11(s2), .in12(k0), .in13(pr), .in14(pr), .in15(ra), .out(Data_Out0), .sel(RegSel0));

  // Other names for the same wires on the sheet: Din[31:0] = reg0DataIn; en = WrReg; sp[31:0] = pr
endmodule
